// Digital circuit Address Decoder.dig as structural Verilog
module Address_Decoder (
  input  E,
  input  R_nW,
  input  A15,
  input  A14,
  input  A13,
  input  A12,
  input  A11,
  input  A10,
  output nBOOT,
  output nSPARE,
  output nEXTRA,
  output nRAM,
  output nPIA1,
  output nPIA2
);

  wire and_1_out, and_2_out, and_3_out, not_1_out, not_2_out, not_3_out, not_4_out, not_5_out, not_6_out;

  not not_1 (not_1_out, A12);
  not not_2 (not_2_out, A11);
  not not_3 (not_3_out, A10);
  not not_4 (not_4_out, A13);
  not not_5 (not_5_out, A14);
  and and_1 (and_1_out, R_nW, E, A15, A14, A13);
  and and_2 (and_2_out, E, R_nW, A15, A14, not_4_out);
  and and_3 (and_3_out, not_4_out, not_5_out, A15, R_nW, E);
  nand nand_1 (nPIA1, A15, not_5_out, A13, not_1_out, not_2_out, not_3_out);
  nand nand_2 (nPIA2, A15, not_5_out, A13, not_1_out, not_2_out, A10);
  nand nand_3 (nRAM, E, not_6_out);
  not not_6 (not_6_out, A15);
  not not_7 (nBOOT, and_1_out);
  not not_8 (nSPARE, and_2_out);
  not not_9 (nEXTRA, and_3_out);

  // Notes on the sheet:
  //   E: Enable
  //   R_nW: Read Not Write
  //   nBOOT: $E000
  //   nSPARE: $C000
  //   nRAM: $0000
endmodule
